# Fritzing sketch U10516045 (saved by Fritzing 0.9.2b)
breadboards: 1

parts:
  Uno = Arduino Uno (Rev3)
  ADXL345 = ADXL345 [package=lga14]
  LED = LED - 3mm [color="Red (633nm)" package="3 mm [THT]"]
  Buzzer = Piezo Speaker

nets:
  N1: Uno.A4/SDA, ADXL345.SDA
  N2: Uno.A5/SCL, ADXL345.SCL
  N3: Uno.D12/MISO, Buzzer.pin2
  N4: Uno.D13/SCK, LED.anode
  GND: Uno.GND, ADXL345.GND, LED.cathode, Buzzer.pin1
  5V: Uno.5V, ADXL345.VDD
